# Fritzing sketch thung-rac-thong-minh (saved by Fritzing 0.9.10b)
breadboards: 2

parts:
  Mod1 = Amica NodeMCU DEVKIT 1.0
  DFRobot_DFPlayer_Mini1 = DFRobot DFPlayer Mini [part_number=DFR0299]
  M2 = Dagu DGServo 9g (Top view) [part_number=RS001B]
  HC-SR04_Sensor_1 = HC-SR04 Ultrasonic Distance Sensor
  HC-SR04_Sensor_2 = HC-SR04 Ultrasonic Distance Sensor
  SP1 = SPEAKER [package=pcb_mount_speaker]

nets:
  GND: Mod1.pin2, Mod1.pin_29, DFRobot_DFPlayer_Mini1.GND-1, DFRobot_DFPlayer_Mini1.GND-2, M2.gnd, HC-SR04_Sensor_1.GND, HC-SR04_Sensor_2.GND
  N1: Mod1.pin6, M2.pulse
  N2: Mod1.pin7, HC-SR04_Sensor_2.ECHO
  N3: Mod1.pin8, HC-SR04_Sensor_1.ECHO
  N4: Mod1.pin_11, HC-SR04_Sensor_1.TRIG
  N5: Mod1.pin_13, DFRobot_DFPlayer_Mini1.TX
  N6: Mod1.pin_14, DFRobot_DFPlayer_Mini1.RX
  N7: Mod1.pin_15, HC-SR04_Sensor_2.TRIG
  VCC: Mod1.pin_17, DFRobot_DFPlayer_Mini1.VCC, M2.vcc, HC-SR04_Sensor_1.VCC, HC-SR04_Sensor_2.VCC
  N8: DFRobot_DFPlayer_Mini1.SPK_1, SP1.+
  N9: DFRobot_DFPlayer_Mini1.SPK_2, SP1.-

notes:
  GPS NEO-6M
  VCC TX RX GND
  [cảm biến đóng mở]
  [cảm biến lượng giác]
